# Fritzing sketch Untitled Sketch (saved by Fritzing 0.9.4)

parts:
  M1 = L293D Motor Driver
  Part1 = Arduino Uno (Rev3)
  BAT1 = BC9VPC [package=bc9vpc]
  M2 = DC Motor
  M3 = DC Motor

nets:
  N1: M1.pin_3, BAT1.V+
  N2: M1.pin_4, Part1.GND, BAT1.V-
  N3: M1.pin_5, Part1.D9_PWM
  N4: M1.pin_6, Part1.D10_PWM/SS
  N5: M1.pin_7, Part1.D11_PWM/MOSI
  N6: M1.pin_8, Part1.D12/MISO
  N7: M1.pin_9, M3.pin_1
  N8: M1.pin_10, M3.pin_2
  N9: M1.pin_11, M2.pin_1
  N10: M1.pin_12, M2.pin_2
